// Logisim project projeto.circ as structural Verilog: 5 circuits, main circuit banco_de_registradores
module main (
);

  wire and_1_out, and_2_out, bnzi, branch, clk, jump, load, mult2, not_1_out, or_1_out, store, tipo_h,
       usa_imm, usa_r0, usa_r3, write, zero;
  wire [1:0] multiplexer_3_out, multiplexer_4_out, ra, rb;
  wire [2:0] func;
  wire [3:0] bit_extender_1_out, multiplexer_6_out, opcode;
  wire [7:0] adder_1_out, adder_2_out, bit_extender_2_out, bit_extender_3_out, dual_port_ram_1_data,
       multiplexer_1_out, multiplexer_2_out, multiplexer_7_out, not_2_out, pc_q, regx, regy, regz, saida_Ula,
       soma_PC;

  // Probe on soma_PC
  // Probe on multiplexer_1_out
  Multiplexer #(.width(8)) multiplexer_1 (.in0(8'h1), .in1(soma_PC), .out(multiplexer_1_out), .sel(or_1_out));
  or or_1 (or_1_out, jump, and_1_out);
  and and_1 (and_1_out, bnzi, not_1_out);
  not not_1 (not_1_out, zero);
  Adder adder_1 (.a(pc_q), .b(multiplexer_1_out), .out(adder_1_out));  // open: cin, cout
  and and_2 (and_2_out, branch, zero);
  // Probe on multiplexer_2_out
  Multiplexer #(.width(8)) multiplexer_2 (.in0(adder_1_out), .in1(regy), .out(multiplexer_2_out), .sel(1'b0));
  Register pc (.D(multiplexer_2_out), .en(1'b1), .clk(clk), .Q(pc_q));  // open: clr
  Clock #(.highDuration(2), .lowDuration(2)) clock_1 (.out(clk));
  Multiplexer #(.width(2)) multiplexer_3 (.in0(ra), .in1(2'b00), .out(multiplexer_3_out), .sel(usa_r0));
  // Probe on {opcode, ra, rb}
  dual_port_ram dual_port_ram_1 (
    .addr(regy), .pc(pc_q), .d(regx), .w(store), .instr({opcode, ra, rb}), .data(dual_port_ram_1_data));
  // Probe on nothing
  Multiplexer #(.width(2)) multiplexer_4 (.in0(multiplexer_3_out), .in1(2'b11), .out(multiplexer_4_out), .sel(usa_r3));
  // Probe on opcode
  // Probe on {ra, rb}
  // Probe on rb
  // Probe on ra
  Multiplexer #(.width(8)) multiplexer_5 (.in0(saida_Ula), .in1(dual_port_ram_1_data), .out(regz), .sel(load));
  assign bit_extender_1_out = {{2{rb[1]}}, rb};  // Bit_Extender bit_extender_1
  controle controle_1 (
    .opcode(opcode), .write(write), .branch(branch), .jump(jump), .bnzi(bnzi), .store(store), .load(load),
    .tipo_h(tipo_h), .usa_imm(usa_imm), .usa_r0(usa_r0), .usa_r3(usa_r3), .mult2(mult2), .func(func));
  // Probe on func
  Multiplexer #(.width(4)) multiplexer_6 (
    .in0({ra, rb}), .in1(bit_extender_1_out), .out(multiplexer_6_out), .sel(tipo_h));
  // Probe on regx
  banco_de_registradores banco_de_registradores_1 (
    .w(write), .Regz(regz), .ra(multiplexer_4_out), .rb(rb), .clk(clk), .regx(regx), .regy(regy));
  // Probe on regy
  assign bit_extender_2_out = {{4{multiplexer_6_out[3]}}, multiplexer_6_out};  // Bit_Extender bit_extender_2
  // Probe on bit_extender_2_out
  assign bit_extender_3_out = {{4{1'b0}}, multiplexer_6_out};  // Bit_Extender bit_extender_3
  assign not_2_out = ~bit_extender_3_out;  // NOT_Gate not_2, 8 bits wide
  Multiplexer #(.width(8)) multiplexer_7 (.in0(regy), .in1(bit_extender_2_out), .out(multiplexer_7_out), .sel(usa_imm));
  Adder adder_2 (.a(not_2_out), .b(8'h1), .out(adder_2_out));  // open: cin, cout
  Multiplexer #(.width(8)) multiplexer_8 (.in0(adder_2_out), .in1(bit_extender_2_out), .out(soma_PC), .sel(jump));
  ULA ula_1 (.Ra(regx), .Rb(multiplexer_7_out), .mult2(mult2), .func(func), .saida_ULA(saida_Ula), .zero(zero));
  // Probe on saida_Ula
endmodule

module banco_de_registradores (
  input  w,
  input  [7:0] Regz,
  input  [1:0] ra,
  input  [1:0] rb,
  input  clk,
  output [7:0] regx,
  output [7:0] regy
);

  wire [7:0] demultiplexer_1_out0, demultiplexer_1_out1, demultiplexer_1_out2, demultiplexer_1_out3, r0_q,
       r1_q, r2_q, r3_q;

  Demultiplexer #(.select(2), .width(8)) demultiplexer_1 (
    .out0(demultiplexer_1_out0), .out1(demultiplexer_1_out1), .out2(demultiplexer_1_out2),
    .out3(demultiplexer_1_out3), .in(Regz), .sel(ra));
  Register r0 (.D(demultiplexer_1_out0), .en(w), .clk(clk), .Q(r0_q));  // open: clr
  Register r2 (.D(demultiplexer_1_out2), .en(w), .clk(clk), .Q(r2_q));  // open: clr
  Register r1 (.D(demultiplexer_1_out1), .en(w), .clk(clk), .Q(r1_q));  // open: clr
  Register r3 (.D(demultiplexer_1_out3), .en(w), .clk(clk), .Q(r3_q));  // open: clr
  Multiplexer #(.select(2), .width(8)) multiplexer_1 (
    .in0(r0_q), .in1(r1_q), .in2(r2_q), .in3(r3_q), .out(regx), .sel(ra));
  Multiplexer #(.select(2), .width(8)) multiplexer_2 (
    .in0(r0_q), .in1(r1_q), .in2(r2_q), .in3(r3_q), .out(regy), .sel(rb));
  // Probe on regx
endmodule

module ULA (
  input  [7:0] Ra,
  input  [7:0] Rb,
  input  mult2,
  input  [2:0] func,
  output [7:0] saida_ULA,
  output zero
);

  wire [7:0] adder_1_out, and_1_out, multiplexer_1_out, not_1_out, or_1_out, shifter_1_out, shifter_2_out,
       shifter_3_out, subtractor_1_out, xor_1_out;

  Multiplexer #(.width(8)) multiplexer_1 (.in0(Rb), .in1(shifter_1_out), .out(multiplexer_1_out), .sel(mult2));
  Shifter shifter_1 (.in(Rb), .\dist (3'b001), .out(shifter_1_out));
  Adder adder_1 (.a(Ra), .b(multiplexer_1_out), .out(adder_1_out));  // open: cin, cout
  Subtractor subtractor_1 (.a(Ra), .b(multiplexer_1_out), .out(subtractor_1_out));  // open: bin, bout
  assign not_1_out = ~Ra;  // NOT_Gate not_1, 8 bits wide
  assign and_1_out = multiplexer_1_out & Ra;  // AND_Gate and_1, 8 bits wide
  assign or_1_out = multiplexer_1_out | Ra;  // OR_Gate or_1, 8 bits wide
  Shifter #(.shift("lr")) shifter_2 (.in(multiplexer_1_out), .\dist (Ra[2:0]), .out(shifter_2_out));
  Shifter #(.shift("lr")) shifter_3 (.\dist (Ra[2:0]), .out(shifter_3_out));  // open: in
  Comparator comparator_1 (.a(multiplexer_1_out), .b({8{1'b0}}), .eq(zero));  // open: gt, lt
  assign xor_1_out = multiplexer_1_out ^ Ra;  // XOR_Gate xor_1, 8 bits wide
  Multiplexer #(.select(3), .width(8)) multiplexer_2 (
    .in0(adder_1_out), .in1(subtractor_1_out), .in2(not_1_out), .in3(and_1_out), .in4(or_1_out),
    .in5(xor_1_out), .in6(shifter_2_out), .in7(shifter_3_out), .out(saida_ULA), .sel(func));
endmodule

module controle (
  input  [3:0] opcode,
  output write,
  output branch,
  output jump,
  output bnzi,
  output store,
  output load,
  output tipo_h,
  output usa_imm,
  output usa_r0,
  output usa_r3,
  output mult2,
  output [2:0] func
);

  wire and_3_out, and_4_out, and_8_out, not_1_out, not_2_out, not_3_out, not_4_out, not_5_out, not_6_out,
       not_7_out, not_8_out, not_9_out, not_10_out, not_11_out, not_12_out, not_13_out, not_14_out,
       not_15_out, not_16_out, not_17_out, or_1_out, or_2_out, or_3_out, or_4_out, or_5_out;

  ROM #(.addrWidth(4), .dataWidth(3)) rom_1 (.addr(opcode), .data(func));
  or or_1 (or_1_out, opcode[1], not_1_out);
  not not_1 (not_1_out, opcode[0]);
  or or_2 (or_2_out, opcode[0], opcode[1], opcode[2], opcode[3]);
  or or_3 (or_3_out, opcode[1], opcode[2], opcode[3]);
  not not_2 (not_2_out, or_3_out);
  or or_4 (or_4_out, opcode[0], opcode[2], opcode[3]);
  not not_3 (not_3_out, or_4_out);
  not not_4 (not_4_out, opcode[0]);
  not not_5 (not_5_out, opcode[1]);
  and and_1 (store, not_4_out, not_5_out, opcode[2], opcode[3]);
  or or_5 (or_5_out, opcode[3], opcode[2], opcode[0]);
  not not_6 (not_6_out, or_5_out);
  not not_7 (not_7_out, opcode[0]);
  and and_2 (tipo_h, not_7_out, opcode[1], opcode[2], opcode[3]);
  and and_3 (and_3_out, opcode[2], not_8_out);
  not not_8 (not_8_out, opcode[3]);
  not not_9 (not_9_out, opcode[1]);
  and and_4 (and_4_out, opcode[0], not_9_out, not_10_out, not_11_out);
  not not_10 (not_10_out, opcode[2]);
  not not_11 (not_11_out, opcode[3]);
  not not_12 (not_12_out, opcode[3]);
  and and_5 (usa_r0, not_12_out, opcode[2], not_13_out);
  not not_13 (not_13_out, opcode[0]);
  not not_14 (not_14_out, opcode[3]);
  and and_6 (usa_r3, not_14_out, opcode[2], not_15_out, opcode[0]);
  not not_15 (not_15_out, opcode[1]);
  not not_16 (not_16_out, opcode[3]);
  and and_7 (mult2, not_16_out, opcode[2], opcode[1], not_17_out);
  not not_17 (not_17_out, opcode[0]);
  or or_6 (write, opcode[3], and_8_out);
  and and_8 (and_8_out, opcode[2], or_1_out);
  not not_18 (branch, or_2_out);
  and and_9 (jump, opcode[0], not_2_out);
  and and_10 (bnzi, not_3_out, opcode[1]);
  and and_11 (load, not_6_out, opcode[1]);
  or or_7 (usa_imm, and_3_out, and_4_out);

  // Notes on the sheet:
  //   contents of rom_1 (hex, n*v repeats v):
  //   9*0 2 3 4 5 0 6 7
endmodule

module dual_port_ram (
  input  [7:0] addr,
  input  [7:0] pc,
  input  [7:0] d,
  input  w,
  output [7:0] instr,
  output [7:0] data
);

  wire clock_1_out, or_1_out;
  wire [7:0] multiplexer_1_out;

  Clock clock_1 (.out(clock_1_out));
  or or_1 (or_1_out, w, clock_1_out);
  Multiplexer #(.width(8)) multiplexer_1 (.in0(addr), .in1(pc), .out(multiplexer_1_out), .sel(clock_1_out));
  RAM #(.asyncread("true")) ram_1 (
    .addr(multiplexer_1_out), .we(or_1_out), .oe(1'b1), .clk(clock_1_out), .din(d), .dout(data));
  Register #(.trigger("falling")) pcbuf (.D(data), .en(1'b1), .clk(clock_1_out), .Q(instr));  // open: clr
endmodule
