// Logisim project projeto.circ as structural Verilog: 10 circuits, main circuit main
module main (
);

  wire and_1_out, and_2_out, and_3_out, and_4_out, and_5_out, and_6_out, bnzi, branch, clk, cmd_v,
       comparator_1_eq, comparator_2_eq, load, not_1_out, not_2_out, not_3_out, or_1_out, reset, store,
       tipo_h, usa_imm, write, zero;
  wire [1:0] multiplexer_5_out, multiplexer_6_out, ra, rb, subtractor_1_out;
  wire [2:0] func;
  wire [3:0] bit_extender_1_out, bit_extender_2_out, multiplexer_3_out, multiplexer_4_out;
  wire [7:0] adder_1_out, adder_2_out, banco_de_registradores_1_regx, imm, multiplexer_1_out,
       multiplexer_2_out, multiplexer_7_out, multiplexer_8_out, multiplexer_9_out, multiplexer_10_out,
       multiplexer_11_out, multiplexer_12_out, multiplexer_13_out, multiplexer_14_out, multiplexer_15_out,
       multiplexer_16_out, multiplier_1_out, ram_1_dout, ram_2_dout, ram_3_dout, ram_4_dout, ram_5_dout,
       register_1_q, regy, ula_1_saida_ula, v_br0_1_regx, v_br0_1_regy, v_br1_1_regx, v_br1_1_regy,
       v_br2_1_regx, v_br2_1_regy, v_br3_1_regx, v_br3_1_regy, vula_1_saida_ula, vula_2_saida_ula,
       vula_3_saida_ula, vula_4_saida_ula;
  wire [7:4] mem_instrucoes_data;

  // Probe on imm
  Multiplier multiplier_1 (.a(imm), .b(8'h2), .out(multiplier_1_out));  // open: cin, cout
  // Probe on multiplier_1_out
  Adder adder_1 (.a(register_1_q), .b(8'h1), .out(adder_1_out), .cin(1'b0));  // open: cout
  and and_1 (and_1_out, bnzi, not_1_out);
  Adder adder_2 (.a(adder_1_out), .b(multiplier_1_out), .out(adder_2_out));  // open: cin, cout
  // Probe on adder_2_out
  // Probe on multiplexer_1_out
  Multiplexer #(.width(8)) multiplexer_1 (
    .in0(adder_1_out), .in1(adder_2_out), .out(multiplexer_1_out), .sel(and_1_out));
  // Probe on not_1_out
  not not_1 (not_1_out, zero);
  Button u_reset (.out(reset));
  Multiplexer #(.width(8)) multiplexer_2 (
    .in0(multiplexer_1_out), .in1(regy), .out(multiplexer_2_out), .sel(and_2_out));
  and and_2 (and_2_out, branch, zero);
  controle controle_1 (
    .opcode(mem_instrucoes_data), .comando_v(cmd_v), .write(write), .load(load), .store(store),
    .branch(branch), .usa_imm(usa_imm), .func(func), .tipo_h(tipo_h), .bnez(bnzi));
  Register register_1 (.D(multiplexer_2_out), .en(1'b1), .clk(clk), .Q(register_1_q), .clr(reset));
  ROM mem_instrucoes (.addr(register_1_q), .data({mem_instrucoes_data, ra, rb}));
  // Probe on {1'b0, ra[1]}
  // Probe on func
  assign bit_extender_1_out = {{1{ra[0]}}, {ra[0], rb}};  // Bit_Extender bit_extender_1
  Multiplexer #(.width(4)) multiplexer_3 (
    .in0({ra, rb}), .in1(bit_extender_2_out), .out(multiplexer_3_out), .sel(tipo_h));
  assign bit_extender_2_out = {{2{rb[1]}}, rb};  // Bit_Extender bit_extender_2
  Multiplexer #(.width(4)) multiplexer_4 (
    .in0(multiplexer_3_out), .in1(bit_extender_1_out), .out(multiplexer_4_out), .sel(bnzi));
  // Probe on ra
  Comparator #(.width(3)) comparator_1 (.a(func), .b(3'b001), .eq(comparator_1_eq));  // open: gt, lt
  or or_1 (or_1_out, comparator_1_eq, comparator_2_eq);
  Comparator #(.width(3)) comparator_2 (.a(func), .b(3'b010), .eq(comparator_2_eq));  // open: gt, lt
  Subtractor #(.width(2)) subtractor_1 (.a(2'b11), .b({1'b0, ra[1]}), .out(subtractor_1_out));  // open: bin, bout
  assign imm = {{4{multiplexer_4_out[3]}}, multiplexer_4_out};  // Bit_Extender bit_extender_3
  Multiplexer #(.width(2)) multiplexer_5 (.in0(ra), .in1(2'b01), .out(multiplexer_5_out), .sel(or_1_out));
  Multiplexer #(.width(2)) multiplexer_6 (
    .in0(multiplexer_5_out), .in1(subtractor_1_out), .out(multiplexer_6_out), .sel(bnzi));
  // Probe on multiplexer_5_out
  Clock #(.highDuration(2), .lowDuration(2), .phaseOffset(1)) clock_1 (.out(clk));
  // Probe on multiplexer_16_out
  // Probe on multiplexer_6_out
  // Probe on rb
  // Probe on multiplexer_7_out
  and and_3 (and_3_out, write, cmd_v);
  // Probe on multiplexer_8_out
  // Probe on multiplexer_9_out
  // Probe on multiplexer_10_out
  and and_4 (and_4_out, write, not_2_out);
  not not_2 (not_2_out, cmd_v);
  V_BR0 v_br0_1 (
    .w(and_3_out), .reset(reset), .Regz(multiplexer_7_out), .ra(multiplexer_5_out), .rb(rb), .clk(clk),
    .regx(v_br0_1_regx), .regy(v_br0_1_regy));
  V_BR1 v_br1_1 (
    .w(and_3_out), .reset(reset), .Regz(multiplexer_8_out), .ra(multiplexer_5_out), .rb(rb), .clk(clk),
    .regx(v_br1_1_regx), .regy(v_br1_1_regy));
  V_BR2 v_br2_1 (
    .w(and_3_out), .reset(reset), .Regz(multiplexer_9_out), .ra(multiplexer_5_out), .rb(rb), .clk(clk),
    .regx(v_br2_1_regx), .regy(v_br2_1_regy));
  Multiplexer #(.width(8)) multiplexer_7 (
    .in0(vula_1_saida_ula), .in1(ram_2_dout), .out(multiplexer_7_out), .sel(load));
  Multiplexer #(.width(8)) multiplexer_8 (
    .in0(vula_2_saida_ula), .in1(ram_3_dout), .out(multiplexer_8_out), .sel(load));
  Multiplexer #(.width(8)) multiplexer_9 (
    .in0(vula_3_saida_ula), .in1(ram_4_dout), .out(multiplexer_9_out), .sel(load));
  Multiplexer #(.width(8)) multiplexer_10 (
    .in0(vula_4_saida_ula), .in1(ram_5_dout), .out(multiplexer_10_out), .sel(load));
  V_BR3 v_br3_1 (
    .w(and_3_out), .reset(reset), .Regz(multiplexer_10_out), .ra(multiplexer_5_out), .rb(rb), .clk(clk),
    .regx(v_br3_1_regx), .regy(v_br3_1_regy));
  // Probe on banco_de_registradores_1_regx
  banco_de_registradores banco_de_registradores_1 (
    .write(and_4_out), .reset(reset), .regz(multiplexer_16_out), .ra(multiplexer_6_out), .rb(rb),
    .clock(clk), .regx(banco_de_registradores_1_regx), .regy(regy));
  // Probe on imm
  // Probe on v_br1_1_regx
  // Probe on v_br2_1_regx
  // Probe on v_br3_1_regx
  // Probe on regy
  // Probe on v_br0_1_regx
  Multiplexer #(.width(8)) multiplexer_11 (.in0(v_br0_1_regy), .in1(imm), .out(multiplexer_11_out), .sel(usa_imm));
  // Probe on multiplexer_12_out
  Multiplexer #(.width(8)) multiplexer_12 (.in0(v_br1_1_regy), .in1(imm), .out(multiplexer_12_out), .sel(usa_imm));
  // Probe on multiplexer_13_out
  Multiplexer #(.width(8)) multiplexer_13 (.in0(v_br2_1_regy), .in1(imm), .out(multiplexer_13_out), .sel(usa_imm));
  // Probe on multiplexer_14_out
  Multiplexer #(.width(8)) multiplexer_14 (.in0(v_br3_1_regy), .in1(imm), .out(multiplexer_14_out), .sel(usa_imm));
  Multiplexer #(.width(8)) multiplexer_15 (.in0(regy), .in1(imm), .out(multiplexer_15_out), .sel(usa_imm));
  // Probe on v_br0_1_regy
  // Probe on vula_1_saida_ula
  VULA vula_1 (.Ra(v_br0_1_regx), .Rb(multiplexer_11_out), .func(func), .saida_ula(vula_1_saida_ula));
  // Probe on vula_2_saida_ula
  VULA vula_2 (.Ra(v_br1_1_regx), .Rb(multiplexer_12_out), .func(func), .saida_ula(vula_2_saida_ula));
  // Probe on vula_3_saida_ula
  // Probe on vula_4_saida_ula
  ULA ula_1 (
    .Ra(banco_de_registradores_1_regx), .Rb(multiplexer_15_out), .func(func), .saida_ula(ula_1_saida_ula),
    .zero(zero));
  VULA vula_3 (.Ra(v_br2_1_regx), .Rb(multiplexer_13_out), .func(func), .saida_ula(vula_3_saida_ula));
  VULA vula_4 (.Ra(v_br3_1_regx), .Rb(multiplexer_14_out), .func(func), .saida_ula(vula_4_saida_ula));
  Multiplexer #(.width(8)) multiplexer_16 (
    .in0(ula_1_saida_ula), .in1(ram_1_dout), .out(multiplexer_16_out), .sel(load));
  and and_5 (and_5_out, store, not_3_out);
  not not_3 (not_3_out, cmd_v);
  // Probe on v_br1_1_regy
  // Probe on v_br3_1_regy
  and and_6 (and_6_out, store, cmd_v);
  // Probe on regy
  RAM #(.asyncread("true")) ram_1 (
    .addr(regy), .we(and_5_out), .oe(1'b1), .clk(clk), .din(banco_de_registradores_1_regx), .dout(ram_1_dout));
  RAM #(.asyncread("true")) ram_2 (
    .addr(v_br0_1_regy), .we(and_6_out), .oe(1'b1), .clk(clk), .din(v_br0_1_regx), .dout(ram_2_dout));
  RAM #(.asyncread("true")) ram_3 (
    .addr(v_br1_1_regy), .we(and_6_out), .oe(1'b1), .clk(clk), .din(v_br1_1_regx), .dout(ram_3_dout));
  RAM #(.asyncread("true")) ram_4 (
    .addr(v_br2_1_regy), .we(and_6_out), .oe(1'b1), .clk(clk), .din(v_br2_1_regx), .dout(ram_4_dout));
  RAM #(.asyncread("true")) ram_5 (
    .addr(v_br3_1_regy), .we(and_6_out), .oe(1'b1), .clk(clk), .din(v_br3_1_regx), .dout(ram_5_dout));
  // Probe on ram_5_dout
  // Probe on ram_3_dout

  // Notes on the sheet:
  //   contents of mem_instrucoes (hex, n*v repeats v):
  //   cc c8 33 49 b4 33 4d 9e c9 cd ef eb f5 fa b8 cd 34 71 4d 3b 21 49 37 22 7d bc ef d9 8e d9 86 cd bc
  //   c9 c9 9e b4 c9 72 71
endmodule

module banco_de_registradores (
  input  write,
  input  reset,
  input  [7:0] regz,
  input  [1:0] ra,
  input  [1:0] rb,
  input  clock,
  output [7:0] regx,
  output [7:0] regy
);

  wire and_1_out, and_2_out, and_3_out, demultiplexer_1_out0, demultiplexer_1_out1, demultiplexer_1_out2,
       demultiplexer_1_out3;
  wire [7:0] register_1_q, register_2_q, register_3_q;

  // Probe on regz
  Demultiplexer #(.select(2)) demultiplexer_1 (
    .out0(demultiplexer_1_out0), .out1(demultiplexer_1_out1), .out2(demultiplexer_1_out2),
    .out3(demultiplexer_1_out3), .in(1'b1), .sel(ra));
  // NoConnect on demultiplexer_1_out0
  Register register_1 (.D(regz), .en(and_1_out), .clk(clock), .Q(register_1_q), .clr(reset));
  and and_1 (and_1_out, write, demultiplexer_1_out2);
  // Probe on register_1_q
  and and_2 (and_2_out, write, demultiplexer_1_out1);
  and and_3 (and_3_out, write, demultiplexer_1_out3);
  Register register_2 (.D(regz), .en(and_2_out), .clk(clock), .Q(register_2_q), .clr(reset));
  Register register_3 (.D(regz), .en(and_3_out), .clk(clock), .Q(register_3_q), .clr(reset));
  // Probe on register_2_q
  // Probe on register_3_q
  Multiplexer #(.select(2), .width(8)) multiplexer_1 (
    .in0({8{1'b0}}), .in1(register_2_q), .in2(register_1_q), .in3(register_3_q), .out(regx), .sel(ra));
  Multiplexer #(.select(2), .width(8)) multiplexer_2 (
    .in0({8{1'b0}}), .in1(register_2_q), .in2(register_1_q), .in3(register_3_q), .out(regy), .sel(rb));
  // Probe on regx

  // Other names for the same wires on the sheet: w = write
endmodule

module ULA (
  input  [7:0] Ra,
  input  [7:0] Rb,
  input  [2:0] func,
  output [7:0] saida_ula,
  output zero
);

  wire adder_1_cout, subtractor_1_bout;
  wire [7:0] adder_1_out, and_1_out, subtractor_1_out;

  // Probe on Rb
  // NoConnect on nothing
  // Probe on Ra
  Adder adder_1 (.a(Ra), .b(Rb), .out(adder_1_out), .cin(1'b0), .cout(adder_1_cout));
  Subtractor subtractor_1 (.a(Ra), .b(Rb), .out(subtractor_1_out), .bin(1'b0), .bout(subtractor_1_bout));
  // NoConnect on subtractor_1_bout
  assign and_1_out = Ra & Rb;  // AND_Gate and_1, 8 bits wide
  // Probe on adder_1_out
  Comparator comparator_1 (.a(Ra), .b({8{1'b0}}), .eq(zero));  // open: gt, lt
  Multiplexer #(.select(3), .width(8)) multiplexer_1 (
    .in0({8{1'b0}}), .in1({Rb[3:0], Ra[3:0]}), .in2({Ra[7:4], Rb[3:0]}), .in3({8{1'b0}}), .in4(adder_1_out),
    .in5(subtractor_1_out), .in6(and_1_out), .in7({8{1'b0}}), .out(saida_ula), .sel(func));
endmodule

module controle (
  input  [3:0] opcode,
  output comando_v,
  output write,
  output load,
  output store,
  output branch,
  output usa_imm,
  output [2:0] func,
  output tipo_h,
  output bnez
);

  wire and_1_out, and_2_out, and_3_out, and_4_out, and_5_out, and_6_out, and_8_out, nor_1_out, not_1_out,
       not_2_out, not_3_out, not_4_out, not_5_out, not_6_out, not_7_out, not_8_out, not_9_out, not_10_out,
       not_11_out, not_12_out, not_14_out, not_15_out, or_1_out, or_2_out;

  not not_1 (not_1_out, opcode[1]);
  not not_2 (not_2_out, opcode[2]);
  not not_3 (not_3_out, opcode[0]);
  not not_4 (not_4_out, opcode[1]);
  and and_1 (and_1_out, opcode[0], not_1_out, not_2_out);
  and and_2 (and_2_out, opcode[0], opcode[1], opcode[2], not_5_out);
  not not_5 (not_5_out, opcode[3]);
  or or_1 (or_1_out, opcode[2], opcode[1], opcode[0]);
  not not_6 (not_6_out, opcode[1]);
  not not_7 (not_7_out, opcode[2]);
  not not_8 (not_8_out, opcode[3]);
  and and_3 (and_3_out, opcode[2], opcode[0]);
  not not_9 (not_9_out, opcode[0]);
  and and_4 (and_4_out, not_9_out, opcode[1], not_10_out);
  not not_10 (not_10_out, opcode[2]);
  and and_5 (and_5_out, opcode[0], opcode[1]);
  and and_6 (and_6_out, opcode[1], opcode[2], not_11_out);
  not not_11 (not_11_out, opcode[3]);
  or or_2 (or_2_out, not_3_out, not_4_out);
  and and_7 (func[2], or_2_out, opcode[2]);
  not not_12 (not_12_out, opcode[0]);
  and and_8 (and_8_out, opcode[1], opcode[3], opcode[2]);
  nor nor_1 (nor_1_out, and_1_out, and_2_out);
  not not_13 (load, or_1_out);
  and and_9 (store, opcode[0], not_6_out, not_7_out);
  and and_10 (branch, not_8_out, opcode[2], opcode[1], opcode[0]);
  or or_3 (func[0], and_3_out, and_4_out);
  or or_4 (func[1], and_5_out, and_6_out);
  and and_11 (tipo_h, not_12_out, and_8_out);
  and and_12 (bnez, and_8_out, opcode[0]);
  and and_13 (write, nor_1_out, not_14_out);
  not not_14 (not_14_out, bnez);
  not not_15 (not_15_out, tipo_h);
  and and_14 (comando_v, opcode[3], not_15_out);

  assign usa_imm = opcode[1];
endmodule

module dualport_ram (
  input  [7:0] addr,
  input  [7:0] pc,
  input  [7:0] d,
  input  w,
  output [7:0] instr,
  output [7:0] data
);

  wire clock_1_out, or_1_out;
  wire [7:0] multiplexer_1_out;

  Clock clock_1 (.out(clock_1_out));
  or or_1 (or_1_out, w, clock_1_out);
  Multiplexer #(.width(8)) multiplexer_1 (.in0(addr), .in1(pc), .out(multiplexer_1_out), .sel(clock_1_out));
  RAM #(.asyncread("true")) trab2 (
    .addr(multiplexer_1_out), .we(or_1_out), .oe(1'b1), .clk(clock_1_out), .din(d), .dout(data));
  Register #(.trigger("falling")) pcbuf (.D(data), .en(1'b1), .clk(clock_1_out), .Q(instr));  // open: clr
endmodule

module V_BR1 (
  input  w,
  input  reset,
  input  [7:0] Regz,
  input  [1:0] ra,
  input  [1:0] rb,
  input  clk,
  output [7:0] regx,
  output [7:0] regy
);

  wire and_1_out, and_2_out, and_3_out, demultiplexer_1_out0, demultiplexer_1_out1, demultiplexer_1_out2,
       demultiplexer_1_out3;
  wire [7:0] r1_q, r2_q, r3_q;

  // Probe on Regz
  Demultiplexer #(.select(2)) demultiplexer_1 (
    .out0(demultiplexer_1_out0), .out1(demultiplexer_1_out1), .out2(demultiplexer_1_out2),
    .out3(demultiplexer_1_out3), .in(1'b1), .sel(ra));
  // NoConnect on demultiplexer_1_out0
  Register r2 (.D(Regz), .en(and_1_out), .clk(clk), .Q(r2_q), .clr(reset));
  and and_1 (and_1_out, w, demultiplexer_1_out2);
  // Probe on r2_q
  and and_2 (and_2_out, w, demultiplexer_1_out1);
  Register r1 (.D(Regz), .en(and_2_out), .clk(clk), .Q(r1_q), .clr(reset));
  Register r3 (.D(Regz), .en(and_3_out), .clk(clk), .Q(r3_q), .clr(reset));
  and and_3 (and_3_out, w, demultiplexer_1_out3);
  // Probe on r1_q
  // Probe on r3_q
  Multiplexer #(.select(2), .width(8)) multiplexer_1 (
    .in0(8'h1), .in1(r1_q), .in2(r2_q), .in3(r3_q), .out(regx), .sel(ra));
  Multiplexer #(.select(2), .width(8)) multiplexer_2 (
    .in0(8'h1), .in1(r1_q), .in2(r2_q), .in3(r3_q), .out(regy), .sel(rb));
  // Probe on regx
endmodule

module V_BR0 (
  input  w,
  input  reset,
  input  [7:0] Regz,
  input  [1:0] ra,
  input  [1:0] rb,
  input  clk,
  output [7:0] regx,
  output [7:0] regy
);

  wire and_1_out, and_2_out, and_3_out, demultiplexer_1_out1, demultiplexer_1_out2, demultiplexer_1_out3;
  wire [7:0] r1_q, r2_q, r3_q;

  // Probe on Regz
  Demultiplexer #(.select(2)) demultiplexer_1 (
    .out1(demultiplexer_1_out1), .out2(demultiplexer_1_out2), .out3(demultiplexer_1_out3), .in(1'b1), .sel(ra));  // open: out0
  Register r2 (.D(Regz), .en(and_1_out), .clk(clk), .Q(r2_q), .clr(reset));
  and and_1 (and_1_out, w, demultiplexer_1_out2);
  // Probe on r2_q
  and and_2 (and_2_out, w, demultiplexer_1_out1);
  Register r1 (.D(Regz), .en(and_2_out), .clk(clk), .Q(r1_q), .clr(reset));
  Register r3 (.D(Regz), .en(and_3_out), .clk(clk), .Q(r3_q), .clr(reset));
  and and_3 (and_3_out, w, demultiplexer_1_out3);
  // Probe on r1_q
  // Probe on r3_q
  Multiplexer #(.select(2), .width(8)) multiplexer_1 (
    .in0({8{1'b0}}), .in1(r1_q), .in2(r2_q), .in3(r3_q), .out(regx), .sel(ra));
  Multiplexer #(.select(2), .width(8)) multiplexer_2 (
    .in0({8{1'b0}}), .in1(r1_q), .in2(r2_q), .in3(r3_q), .out(regy), .sel(rb));
  // Probe on regx
endmodule

module V_BR2 (
  input  w,
  input  reset,
  input  [7:0] Regz,
  input  [1:0] ra,
  input  [1:0] rb,
  input  clk,
  output [7:0] regx,
  output [7:0] regy
);

  wire and_1_out, and_2_out, and_3_out, demultiplexer_1_out1, demultiplexer_1_out2, demultiplexer_1_out3;
  wire [7:0] r1_q, r2_q, r3_q;

  // Probe on Regz
  Demultiplexer #(.select(2)) demultiplexer_1 (
    .out1(demultiplexer_1_out1), .out2(demultiplexer_1_out2), .out3(demultiplexer_1_out3), .in(1'b1), .sel(ra));  // open: out0
  Register r2 (.D(Regz), .en(and_1_out), .clk(clk), .Q(r2_q), .clr(reset));
  and and_1 (and_1_out, w, demultiplexer_1_out2);
  // Probe on r2_q
  and and_2 (and_2_out, w, demultiplexer_1_out1);
  Register r1 (.D(Regz), .en(and_2_out), .clk(clk), .Q(r1_q), .clr(reset));
  Register r3 (.D(Regz), .en(and_3_out), .clk(clk), .Q(r3_q), .clr(reset));
  and and_3 (and_3_out, w, demultiplexer_1_out3);
  // Probe on r1_q
  // Probe on r3_q
  Multiplexer #(.select(2), .width(8)) multiplexer_1 (
    .in0(8'h2), .in1(r1_q), .in2(r2_q), .in3(r3_q), .out(regx), .sel(ra));
  // Probe on ra
  Multiplexer #(.select(2), .width(8)) multiplexer_2 (
    .in0(8'h2), .in1(r1_q), .in2(r2_q), .in3(r3_q), .out(regy), .sel(rb));
  // Probe on rb
  // Probe on regx
  // Probe on regy
endmodule

module V_BR3 (
  input  w,
  input  reset,
  input  [7:0] Regz,
  input  [1:0] ra,
  input  [1:0] rb,
  input  clk,
  output [7:0] regx,
  output [7:0] regy
);

  wire and_1_out, and_2_out, and_3_out, demultiplexer_1_out1, demultiplexer_1_out2, demultiplexer_1_out3;
  wire [7:0] r1_q, r2_q, r3_q;

  // Probe on Regz
  Demultiplexer #(.select(2)) demultiplexer_1 (
    .out1(demultiplexer_1_out1), .out2(demultiplexer_1_out2), .out3(demultiplexer_1_out3), .in(1'b1), .sel(ra));  // open: out0
  Register r2 (.D(Regz), .en(and_1_out), .clk(clk), .Q(r2_q), .clr(reset));
  and and_1 (and_1_out, w, demultiplexer_1_out2);
  // Probe on r2_q
  and and_2 (and_2_out, w, demultiplexer_1_out1);
  Register r1 (.D(Regz), .en(and_2_out), .clk(clk), .Q(r1_q), .clr(reset));
  Register r3 (.D(Regz), .en(and_3_out), .clk(clk), .Q(r3_q), .clr(reset));
  and and_3 (and_3_out, w, demultiplexer_1_out3);
  // Probe on r1_q
  // Probe on r3_q
  Multiplexer #(.select(2), .width(8)) multiplexer_1 (
    .in0(8'h3), .in1(r1_q), .in2(r2_q), .in3(r3_q), .out(regx), .sel(ra));
  Multiplexer #(.select(2), .width(8)) multiplexer_2 (
    .in0(8'h3), .in1(r1_q), .in2(r2_q), .in3(r3_q), .out(regy), .sel(rb));
  // Probe on regx
endmodule

module VULA (
  input  [7:0] Ra,
  input  [7:0] Rb,
  input  [2:0] func,
  output [7:0] saida_ula
);

  wire adder_1_cout;
  wire [7:0] adder_1_out, and_1_out, subtractor_1_out;

  // Probe on Ra
  Adder adder_1 (.a(Ra), .b(Rb), .out(adder_1_out), .cin(1'b0), .cout(adder_1_cout));
  Subtractor subtractor_1 (.a(Ra), .b(Rb), .out(subtractor_1_out), .bin(1'b0));  // open: bout
  assign and_1_out = Ra & Rb;  // AND_Gate and_1, 8 bits wide
  Multiplexer #(.select(3), .width(8)) multiplexer_1 (
    .in0({8{1'b0}}), .in1({Rb[3:0], Ra[3:0]}), .in2({Ra[7:4], Rb[3:0]}), .in3({8{1'b0}}), .in4(adder_1_out),
    .in5(subtractor_1_out), .in6(and_1_out), .in7({8{1'b0}}), .out(saida_ula), .sel(func));
endmodule
